// Logisim project control_logic.circ as structural Verilog: 2 circuits, main circuit control_logic
module control_logic (
  input  [31:0] inst,
  input  BrEq,
  input  BrLt,
  output PCSel,
  output RegWEn,
  output [2:0] ImmSel,
  output BrUn,
  output ASel,
  output BSel,
  output [3:0] ALUSel,
  output [3:0] MemRW,
  output [1:0] WBSel,
  output CSRSel,
  output CSRWen
);

  ROM #(.addrWidth(12), .dataWidth(20)) rom_1 (
    .addr({inst[6:2], inst[14:12], inst[30], inst[25], BrEq, BrLt}),
    .data({PCSel, RegWEn, ImmSel, BrUn, ASel, BSel, ALUSel, MemRW, WBSel, CSRSel, CSRWen}));

  // Other names for the same wires on the sheet: MulSel = inst[25]; SignBit = inst[30]; Funct3[2:0] = inst[14:12];
  //   Opcode_2_6[4:0] = inst[6:2]

  // Notes on the sheet:
  //   INPUTS to your circuit
  //   DON'T CHANGE THE LOCATIONS OF THE INPUTS AND OUTPUTS!
  //   OUTPUT from your circuit
  //   contents of rom_1 (hex, n*v repeats v):
  //   49000 0 0 0 49000 0 0 0 49000 0 0 0 49000 0 0 0 49000 0 0 0 49000 0 0 0 49000 0 0 0 49000 0 0 0
  //   49000 0 0 0 49000 0 0 0 49000 0 0 0 49000 467*0 49004 0 0 0 49004 0 0 0 49004 0 0 0 49004 0 0 0
  //   49604 0 0 0 49604 0 0 0 49604 0 0 0 49604 0 0 0 49704 0 0 0 49704 0 0 0 49704 0 0 0 49704 19*0 49304
  //   0 0 0 49304 0 0 0 49304 0 0 0 49304 0 0 0 49404 0 0 0 49404 0 0 0 49504 0 0 0 49504 0 0 0 49204 0 0
  //   0 49204 0 0 0 49204 0 0 0 49204 0 0 0 49104 0 0 0 49104 0 0 0 49104 0 0 0 49104 387*0 11010 0 0 0
  //   11010 0 0 0 11010 0 0 0 11010 0 0 0 11030 0 0 0 11030 0 0 0 11030 0 0 0 11030 0 0 0 110f0 0 0 0
  //   110f0 0 0 0 110f0 0 0 0 110f0 467*0 40004 0 0 0 40a04 0 0 0 40c04 7*0 40604 0 0 0 40e04 11*0 40704
  //   19*0 40b04 11*0 40304 15*0 40404 7*0 40504 7*0 40204 15*0 40104
endmodule

module ALU_Decode (
  input  [2:0] funct3,
  input  mul_Sel,
  input  SignBit,
  output [3:0] ALUSel
);

  wire [3:0] addOrSubOrMul, sllOrMulh, sltuOrMulhu, sra_l_0;

  Multiplexer #(.enable("false"), .width(4)) multiplexer_1 (.in0(4'b0100), .in1(4'b0101), .out(sra_l_0), .sel(SignBit));
  Multiplexer #(.enable("false"), .select(3), .width(4)) multiplexer_2 (
    .in0(addOrSubOrMul), .in1(sllOrMulh), .in2(4'b0111), .in3(sltuOrMulhu), .in4(4'b0011), .in5(sra_l_0),
    .in6(4'b0010), .in7(4'b0001), .out(ALUSel), .sel(funct3));
  Multiplexer #(.enable("false"), .select(2), .width(4)) multiplexer_3 (
    .in0(4'b0000), .in1(4'b1010), .in2(4'b1100), .out(addOrSubOrMul), .sel({SignBit, mul_Sel}));  // open: in3
  Multiplexer #(.enable("false"), .width(4)) multiplexer_4 (
    .in0(4'b0110), .in1(4'b1110), .out(sllOrMulh), .sel(mul_Sel));
  Multiplexer #(.enable("false"), .width(4)) multiplexer_5 (
    .in0(4'b0111), .in1(4'b1011), .out(sltuOrMulhu), .sel(mul_Sel));

  // Other names for the same wires on the sheet: MS = mul_Sel; S = SignBit
endmodule
