// Logisim project cpu.circ as structural Verilog: 3 circuits, main circuit cpu
module cpu (
  input  clk,
  input  [31:0] INSTRUCTION,
  input  [31:0] READ_DATA,
  output [31:0] WRITE_ADDRESS,
  output [31:0] PROGRAM_COUNTER,
  output [31:0] ra,
  output [31:0] sp,
  output [31:0] t0,
  output [31:0] t1,
  output [31:0] t2,
  output [31:0] s0,
  output [31:0] s1,
  output [31:0] a0,
  output [31:0] tohost,
  output [3:0] WRITE_ENABLE,
  output [31:0] WRITE_DATA
);

  wire RegWEn;
  wire [3:0] ALUSel;
  wire [31:0] adder_1_out, Immediate, rs1_Value, rs2_Value, WriteToReg;

  Adder #(.width(32)) adder_1 (.a(PROGRAM_COUNTER), .b(32'h4), .out(adder_1_out));  // open: cin, cout
  Register #(.width(32)) PC (.D(adder_1_out), .clk(clk), .Q(PROGRAM_COUNTER));  // open: en, clr
  control_logic control_logic_1 (
    .RegWEn(RegWEn), .ALUSel(ALUSel), .inst(INSTRUCTION));  // open: CSRWen, PCSel, ImmSel, BrUn, ASel, BSel, MemRW, WBSel, CSRSel, BrEq, BrLt
  imm_gen imm_gen_1 (.inst(INSTRUCTION), .imm(Immediate));  // open: ImmSel
  regfile regfile_1 (
    .rs1(INSTRUCTION[19:15]), .rs2(INSTRUCTION[24:20]), .rd(INSTRUCTION[11:7]), .Write_Data(WriteToReg),
    .RegWEn(RegWEn), .clk(clk), .ra(ra), .sp(sp), .t0(t0), .t1(t1), .t2(t2), .s0(s0), .s1(s1), .a0(a0),
    .Read_Data_1(rs1_Value), .Read_Data_2(rs2_Value));
  // branch_comp branch_comp_1: pin names not known
  alu alu_1 (.Result(WriteToReg), .A(rs1_Value), .B(Immediate), .ALUSel(ALUSel));
  csr csr_1 (.tohost(tohost));  // open: CSR_address, CSR_din, CSR_WE, clk

  // Notes on the sheet:
  //   Output to IMEM
  //   IMEM (do **NOT** move this)
  //   Inputs from IMEM
  //   It is OK to move the PC, RegFile, ALU, MEM, Branch Comp, Imm Gen, and Control Logic to wherever is most convenient for you when constructing your CPU, and to delete this text
  //   Inputs/Outputs for testing. Do **NOT** move these.
  //   Outputs To DMEM
  //   DMEM (do **NOT** move this)
  //   Inputs From DMEM
endmodule

module I_Type_Decode (
  input  [31:0] Instruction,
  output [4:0] rd,
  output [3:0] ALUSel,
  output [4:0] rs1
);

  Decode_ALU decode_alu_1 (.funct3(Instruction[14:12]), .srl_sra(Instruction[30]), .ALUSel(ALUSel));

  assign rd = Instruction[11:7];
  assign rs1 = Instruction[19:15];
endmodule

module Decode_ALU (
  input  [2:0] funct3,
  input  srl_sra,
  output [3:0] ALUSel
);

  wire [3:0] sra_l_0;

  Multiplexer #(.enable("false"), .select(3), .width(4)) multiplexer_1 (
    .in0(4'b0000), .in1(4'b0110), .in2(4'b0111), .in3(4'b0111), .in4(4'b0011), .in5(sra_l_0), .in6(4'b0010),
    .in7(4'b0001), .out(ALUSel), .sel(funct3));
  Multiplexer #(.enable("false"), .width(4)) multiplexer_2 (.in0(4'b0100), .in1(4'b0101), .out(sra_l_0), .sel(srl_sra));
endmodule
