// Logisim project imm_gen.circ as structural Verilog: 1 circuit, main circuit imm_gen
module imm_gen (
  input  [31:0] inst,
  input  [2:0] ImmSel,
  output [31:0] imm
);

  wire [11:11] S_Imm;
  wire [31:0] I_Imm;
  wire [31:1] B_Imm;

  assign I_Imm = {{20{inst[31]}}, inst[31:20]};  // Bit_Extender bit_extender_1
  assign {B_Imm[31:12], S_Imm[11], B_Imm[10:1], B_Imm[11]} = {{20{inst[31]}}, {inst[31:25], inst[11:7]}};  // Bit_Extender bit_extender_2
  Multiplexer #(.enable("false"), .select(3), .width(32)) multiplexer_1 (
    .in0({32{1'b0}}), .in1(I_Imm), .in2({B_Imm[31:12], S_Imm[11], B_Imm[10:1], B_Imm[11]}),
    .in3({B_Imm, 1'b0}), .in4({inst[31:12], {12{1'b0}}}), .out(imm), .sel(ImmSel));  // open: in5, in6, in7

  // Other names for the same wires on the sheet: S_Imm (some bits) = {B_Imm[31:12], B_Imm[10:1], B_Imm[11]};
  //   inst_7 = B_Imm[11]; Immediate[31:0] = imm; U_Imm[31:12] = inst[31:12]

  // Notes on the sheet:
  //   INPUTS to your circuit
  //   DON'T CHANGE THE LOCATIONS OF THE INPUTS AND OUTPUTS!
  //   OUTPUT from your circuit
endmodule
