// Logisim project regfile.circ as structural Verilog: 2 circuits, main circuit regfile
module regfile (
  input  [4:0] rs1,
  input  [4:0] rs2,
  input  [4:0] rd,
  input  [31:0] Write_Data,
  input  RegWEn,
  input  clk,
  output [31:0] ra,
  output [31:0] sp,
  output [31:0] t0,
  output [31:0] t1,
  output [31:0] t2,
  output [31:0] s0,
  output [31:0] s1,
  output [31:0] a0,
  output [31:0] Read_Data_1,
  output [31:0] Read_Data_2
);


  // Other names for the same wires on the sheet: read_data1[31:0] = Read_Data_1; read_data2[31:0] = Read_Data_2;
  //   read_reg1[4:0] = rs1; read_reg2[4:0] = rs2; write_en = RegWEn; write_reg[4:0] = rd

  // Notes on the sheet:
  //   INPUTS to your circuit
  //   DON'T CHANGE THE LOCATIONS OF THE INPUTS AND OUTPUTS!
  //   These are DEBUG/TEST outputs from your circuit.
  //   OUTPUTS from your circuit
endmodule

module AllRegs (
  input  [31:0] WriteData,
  input  WEn0,
  input  in_3,
  input  in_4,
  input  in_5,
  input  in_6,
  input  in_7,
  input  in_8,
  input  in_9,
  input  Clk,
  input  in_11,
  input  in_12,
  input  in_13,
  input  in_14,
  input  in_15,
  input  in_16,
  input  in_17,
  input  in_18,
  input  in_19,
  input  in_20,
  input  in_21,
  input  in_22,
  input  in_23,
  input  in_24,
  input  in_25,
  input  in_26,
  input  in_27,
  input  in_28,
  input  in_29,
  input  in_30,
  input  in_31,
  input  in_32,
  input  in_33,
  input  in_34,
  output [31:0] ReadData0,
  output [31:0] ReadData1,
  output [31:0] ReadData2,
  output [31:0] ReadData3,
  output [31:0] ReadData4,
  output [31:0] ReadData5,
  output [31:0] ReadData6,
  output [31:0] ReadData7,
  output [31:0] ReadData8,
  output [31:0] ReadData9,
  output [31:0] ReadData10,
  output [31:0] ReadData11,
  output [31:0] ReadData12,
  output [31:0] ReadData13,
  output [31:0] ReadData14,
  output [31:0] ReadData15,
  output [31:0] ReadData16,
  output [31:0] ReadData17,
  output [31:0] ReadData18,
  output [31:0] ReadData19,
  output [31:0] ReadData20,
  output [31:0] ReadData21,
  output [31:0] ReadData22,
  output [31:0] ReadData23,
  output [31:0] ReadData24,
  output [31:0] ReadData25,
  output [31:0] ReadData26,
  output [31:0] ReadData27,
  output [31:0] ReadData28,
  output [31:0] ReadData29,
  output [31:0] ReadData30,
  output [31:0] ReadData31
);

  Register #(.width(32)) x0 (.D(WriteData), .en(WEn0), .clk(Clk), .Q(ReadData0));  // open: clr
  Register #(.width(32)) register_1 (.D(WriteData), .en(in_11), .clk(Clk), .Q(ReadData8));  // open: clr
  Register #(.width(32)) register_2 (.D(WriteData), .en(in_19), .clk(Clk), .Q(ReadData16));  // open: clr
  Register #(.width(32)) register_3 (.D(WriteData), .en(in_27), .clk(Clk), .Q(ReadData24));  // open: clr
  Register #(.width(32)) register_4 (.D(WriteData), .en(in_3), .clk(Clk), .Q(ReadData1));  // open: clr
  Register #(.width(32)) register_5 (.D(WriteData), .en(in_12), .clk(Clk), .Q(ReadData9));  // open: clr
  Register #(.width(32)) register_6 (.D(WriteData), .en(in_20), .clk(Clk), .Q(ReadData17));  // open: clr
  Register #(.width(32)) register_7 (.D(WriteData), .en(in_28), .clk(Clk), .Q(ReadData25));  // open: clr
  Register #(.width(32)) register_8 (.D(WriteData), .en(in_4), .clk(Clk), .Q(ReadData2));  // open: clr
  Register #(.width(32)) register_9 (.D(WriteData), .en(in_13), .clk(Clk), .Q(ReadData10));  // open: clr
  Register #(.width(32)) register_10 (.D(WriteData), .en(in_21), .clk(Clk), .Q(ReadData18));  // open: clr
  Register #(.width(32)) register_11 (.D(WriteData), .en(in_29), .clk(Clk), .Q(ReadData26));  // open: clr
  Register #(.width(32)) register_12 (.D(WriteData), .en(in_5), .clk(Clk), .Q(ReadData3));  // open: clr
  Register #(.width(32)) register_13 (.D(WriteData), .en(in_14), .clk(Clk), .Q(ReadData11));  // open: clr
  Register #(.width(32)) register_14 (.D(WriteData), .en(in_22), .clk(Clk), .Q(ReadData19));  // open: clr
  Register #(.width(32)) register_15 (.D(WriteData), .en(in_30), .clk(Clk), .Q(ReadData27));  // open: clr
  Register #(.width(32)) register_16 (.D(WriteData), .en(in_6), .clk(Clk), .Q(ReadData4));  // open: clr
  Register #(.width(32)) register_17 (.D(WriteData), .en(in_15), .clk(Clk), .Q(ReadData12));  // open: clr
  Register #(.width(32)) register_18 (.D(WriteData), .en(in_23), .clk(Clk), .Q(ReadData20));  // open: clr
  Register #(.width(32)) register_19 (.D(WriteData), .en(in_31), .clk(Clk), .Q(ReadData28));  // open: clr
  Register #(.width(32)) register_20 (.D(WriteData), .en(in_7), .clk(Clk), .Q(ReadData5));  // open: clr
  Register #(.width(32)) register_21 (.D(WriteData), .en(in_16), .clk(Clk), .Q(ReadData13));  // open: clr
  Register #(.width(32)) register_22 (.D(WriteData), .en(in_24), .clk(Clk), .Q(ReadData21));  // open: clr
  Register #(.width(32)) register_23 (.D(WriteData), .en(in_32), .clk(Clk), .Q(ReadData29));  // open: clr
  Register #(.width(32)) register_24 (.D(WriteData), .en(in_8), .clk(Clk), .Q(ReadData6));  // open: clr
  Register #(.width(32)) register_25 (.D(WriteData), .en(in_17), .clk(Clk), .Q(ReadData14));  // open: clr
  Register #(.width(32)) register_26 (.D(WriteData), .en(in_25), .clk(Clk), .Q(ReadData22));  // open: clr
  Register #(.width(32)) register_27 (.D(WriteData), .en(in_33), .clk(Clk), .Q(ReadData30));  // open: clr
  Register #(.width(32)) register_28 (.D(WriteData), .en(in_9), .clk(Clk), .Q(ReadData7));  // open: clr
  Register #(.width(32)) register_29 (.D(WriteData), .en(in_18), .clk(Clk), .Q(ReadData15));  // open: clr
  Register #(.width(32)) register_30 (.D(WriteData), .en(in_26), .clk(Clk), .Q(ReadData23));  // open: clr
  Register #(.width(32)) register_31 (.D(WriteData), .en(in_34), .clk(Clk), .Q(ReadData31));  // open: clr

  // Other names for the same wires on the sheet: Clock = Clk; WriteToReg[31:0] = WriteData
endmodule
