// Logisim project Test.circ as structural Verilog: 3 circuits, main circuit main
module main (
  output [31:0] out_1,
  output [31:0] out_2
);

  Multiple multiple_1 (.in_1(32'h2), .in_2(32'h80000000), .out_3(out_1), .out_4(out_2));
endmodule

module Extend (
  input  [31:0] in_1,
  output [7:0] EightBits,
  output [63:0] out_3,
  output [7:0] Output24_31
);

  Adder adder_1 (.a(in_1[7:0]), .b(in_1[15:8]), .out(EightBits));  // open: cin, cout
  assign out_3 = {{32{in_1[31]}}, in_1};  // Bit_Extender bit_extender_1

  assign Output24_31 = in_1[31:24];

  // Other names for the same wires on the sheet: Bits16_23[7:0] = in_1[23:16]; Bits24_31[7:0] = in_1[31:24]
endmodule

module Multiple (
  input  [31:0] in_1,
  input  [31:0] in_2,
  output [31:0] out_3,
  output [31:0] out_4
);

  Multiplier #(.mode("twosComplement"), .width(32)) multiplier_1 (
    .a(in_1), .b(in_2), .out(out_3), .cout(out_4));  // open: cin
endmodule
